# Fritzing sketch board (saved by Fritzing 1.0.2b)
breadboards: 2

parts:
  M1 = ESP32-S2-DevKitC-1 [part_number=ESP32-S2-DevKitC-1]
  SD_card_module1 = SD Card Module
  Componente1 = PN532 Elechouse RFID NFC Module V3
  Componente2 = GMT020-02 TFT Display
  S1 = Pushbutton [package="[SMD]"]
  S2 = Pushbutton [package="[SMD]"]
  S3 = Pushbutton [package="[SMD]"]
  S4 = Pushbutton [package="[SMD]"]
  S5 = Pushbutton [package="[SMD]"]
  LoRa_Module1 = Ra-01 - LoRa Module SX1278 [part_number=SX1278]

nets:
  3.3V: M1.pin_1, M1.pin_2, SD_card_module1.+3.3, Componente1.VCC, Componente2.3.3V, LoRa_Module1.3.3V
  N1: M1.pin_5, Componente2.DC
  N2: M1.pin_8, LoRa_Module1.DIO2
  N3: M1.pin_9, LoRa_Module1.DIO1
  N4: M1.pin_12, Componente1.SDA
  N5: M1.pin_15, Componente1.SCL
  N6: M1.pin_16, Componente2.CS
  N7: M1.pin_17, Componente2.SDA(MOSI)
  N8: M1.pin_19, Componente2.SCL(SCLK)
  GND: M1.pin_22, M1.pin_23, M1.pin_24, M1.pin_28, M1.pin_36, M1.pin_37, M1.pin_38, M1.pin_39, M1.pin_44, SD_card_module1.GND, Componente1.GND, Componente2.GND, S1.Pin_3, S1.Pin_4, S2.Pin_3, S2.Pin_4, S3.Pin_3, S3.Pin_4, S4.Pin_3, S4.Pin_4, S5.Pin_3, S5.Pin_4, LoRa_Module1.GND
  N9: M1.pin_27, SD_card_module1.CS
  N10: M1.pin_32, SD_card_module1.MOSI, LoRa_Module1.MOSI
  N11: M1.pin_33, SD_card_module1.MISO, LoRa_Module1.MISO
  N12: M1.pin_34, SD_card_module1.SCK, LoRa_Module1.SCK
  N13: S1.Pin_1, S1.Pin_2
  N14: S2.Pin_1, S2.Pin_2
  N15: S3.Pin_1, S3.Pin_2
  N16: S4.Pin_1, S4.Pin_2
  N17: S5.Pin_1, S5.Pin_2

notes:
  PN532 in I2C mode
  to SPI pin
  CS: pin 21
  UP-DOWN-LEFT-RIGHT-OK
  From left to right -->
  to SPI pin
  CS: pin 10

custom parts:
  ESP32-S2-DevKitC-1: ESP32-S2-DevKitC-1 is an entry-level development board based on ESP32-S2-SOLO (on-board PCB antenna). It is based on the ESP32 microcontroller that boasts Wifi, Bluetooth, Ethernet and Low Power support all in a single chip. (vanepp) Feb 2022: converted to ESP32-S2-DevKitC-1. This module is 44pins long (2x22) and 11 pins width.
  SD Card Module: SD Card Module Slot Socket Reader For Arduino ARM MCU
  PN532 Elechouse RFID NFC Module V3: NFC is a popular technology in recent years. We often heard this work while smart phone company such as Samsung or HTC introduces their latest high-end phones. Almost all the high-end phone in the market support NFC. Near field communication (NFC) is a set of standards for smart phones and similar devices to establish radio communication with each other by touching them together or bringing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
  GMT020-02 TFT Display: TFT Display 240x320 with ST7789 or compatible driver, SPI bus. This part is made from Adafruit ST7789 2.0 display.
  Ra-01 - LoRa Module SX1278: The Ra-01 LoRa Module featuring the SX1278 engine by Semtech. Module by AI-Thinker. Module (Ra-01) specifications from: https://www.banggood.com/Ra-01-Smart-Electronics-SX1278-LoRa-Spread-Spectrum-Wireless-Module-Ultra-Far-10KM-433M-p-1130769.html Description: Power supply: DC1.8-3.7V(3.3V) Chip: SX1278 Frequency: 433Mhz Operating temperature: -40~+85°C On Sheild Description (may vary by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
