# Fritzing sketch capibara_arduino_nano_esp32 (saved by Fritzing 1.0.2b)
breadboards: 1

parts:
  A1 = Arduino Nano ESP32
  Part1 = GMT020-02 TFT Display
  S1 = Pushbutton [package="[THT]"]
  S2 = Pushbutton [package="[THT]"]
  S3 = Pushbutton [package="[THT]"]
  S4 = Pushbutton [package="[THT]"]
  S5 = Pushbutton [package="[THT]"]
  Part2 = PN532 Elechouse RFID NFC Module V3
  SD_card_module1 = SD Card Module
  LoRa_Module1 = Ra-01 - LoRa Module SX1278 [part_number=SX1278]

nets:
  N1: A1.Pin_1, SD_card_module1.SCK, LoRa_Module1.SCK
  3.3V: A1.Pin_2, Part1.3.3V, SD_card_module1.+3.3, LoRa_Module1.3.3V
  N2: A1.Pin_5, S1.Pin_1, S1.Pin_2
  GND: A1.Pin_6, A1.Pin_14, A1.Pin_19, Part1.GND, S1.Pin_3, S1.Pin_4, S2.Pin_3, S2.Pin_4, S3.Pin_3, S3.Pin_4, S4.Pin_3, S4.Pin_4, S5.Pin_3, S5.Pin_4, SD_card_module1.GND#0, LoRa_Module1.GND
  N3: A1.Pin_7, S5.Pin_1, S5.Pin_2
  N4: A1.Pin_8, Part2.SCL
  N5: A1.Pin_9, Part2.SDA
  N6: A1.Pin_10, S2.Pin_1, S2.Pin_2
  N7: A1.Pin_11, S4.Pin_1, S4.Pin_2
  N8: A1.Pin_20, Part1.SCL(SCLK)
  N9: A1.Pin_21, LoRa_Module1.DIO1
  N10: A1.Pin_22, Part1.SDA(MOSI)
  N11: A1.Pin_23, Part1.CS
  N12: A1.Pin_24, Part1.DC
  N13: A1.Pin_26, LoRa_Module1.DIO2
  N14: A1.Pin_27, LoRa_Module1.NSS
  N15: A1.Pin_28, SD_card_module1.CS
  N16: A1.Pin_29, SD_card_module1.MOSI, LoRa_Module1.MOSI
  N17: A1.Pin_30, SD_card_module1.MISO, LoRa_Module1.MISO
  N18: S3.Pin_1, S3.Pin_2

custom parts:
  Arduino Nano ESP32: Arduino® Nano ESP32 tht.
  GMT020-02 TFT Display: TFT Display 240x320 with ST7789 or compatible driver, SPI bus. This part is made from Adafruit ST7789 2.0 display.
  PN532 Elechouse RFID NFC Module V3: NFC is a popular technology in recent years. We often heard this work while smart phone company such as Samsung or HTC introduces their latest high-end phones. Almost all the high-end phone in the market support NFC. Near field communication (NFC) is a set of standards for smart phones and similar devices to establish radio communication with each other by touching them together or bringing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
  SD Card Module: SD Card Module Slot Socket Reader For Arduino ARM MCU
  Ra-01 - LoRa Module SX1278: The Ra-01 LoRa Module featuring the SX1278 engine by Semtech. Module by AI-Thinker. Module (Ra-01) specifications from: https://www.banggood.com/Ra-01-Smart-Electronics-SX1278-LoRa-Spread-Spectrum-Wireless-Module-Ultra-Far-10KM-433M-p-1130769.html Description: Power supply: DC1.8-3.7V(3.3V) Chip: SX1278 Frequency: 433Mhz Operating temperature: -40~+85°C On Sheild Description (may vary by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
